// Logisim project ex5.circ as structural Verilog: 5 circuits, main circuit rotr
module rotr (
  input  [15:0] A,
  input  [3:0] B,
  output [15:0] Out1
);

  wire [1:0] low2;
  wire [3:0] low4;
  wire [7:0] high8, low8;
  wire [11:0] high12;
  wire [13:0] high14;

  Multiplexer #(.enable("false"), .width(16)) multiplexer_1 (
    .in0(A), .in1({A[0], A[15:1]}), .out({high14, low2}), .sel(B[0]));
  Multiplexer #(.enable("false"), .width(16)) multiplexer_2 (
    .in0({high14, low2}), .in1({low2, high14}), .out({high12, low4}), .sel(B[1]));
  Multiplexer #(.enable("false"), .width(16)) multiplexer_3 (
    .in0({high12, low4}), .in1({low4, high12}), .out({high8, low8}), .sel(B[2]));
  Multiplexer #(.enable("false"), .width(16)) multiplexer_4 (
    .in0({high8, low8}), .in1({low8, high8}), .out(Out1), .sel(B[3]));

  // Other names for the same wires on the sheet: high[14:0] = A[15:1]; low = A[0]; bit0 = B[0]; bit1 = B[1];
  //   bit2 = B[2]; bit3 = B[3]

  // Notes on the sheet:
  //   PUT CIRCUITRY HERE
endmodule

module rot8 (
  input  [15:0] in_1,
  output [15:0] out_2
);


  // Notes on the sheet:
  //   PUT CIRCUITRY HERE
endmodule

module rot4 (
  input  [15:0] in_1,
  output [15:0] out_2
);


  // Notes on the sheet:
  //   PUT CIRCUITRY HERE
endmodule

module rot2 (
  input  [15:0] in_1,
  output [15:0] out_2
);


  // Notes on the sheet:
  //   PUT CIRCUITRY HERE
endmodule

module rot1 (
  input  [15:0] in_1,
  output [15:0] out_2
);


  // Notes on the sheet:
  //   PUT CIRCUITRY HERE
endmodule
