// Logisim project control_logic.circ as structural Verilog: 1 circuit, main circuit control_logic
module control_logic (
  input  [31:0] inst,
  input  BrEq,
  input  BrLt,
  output PCSel,
  output RegWEn,
  output [2:0] ImmSel,
  output BrUn,
  output ASel,
  output BSel,
  output [3:0] ALUSel,
  output MemRW,
  output [1:0] WBSel,
  output CSRSel,
  output CSRWen
);

  wire brSel, or_1_out, RomPCSel;

  ROM #(.addrWidth(12), .dataWidth(18)) rom_1 (
    .addr({inst[30], inst[25], inst[14:12], inst[6:0]}),
    .data({brSel, CSRWen, CSRSel, WBSel, MemRW, ALUSel, BSel, ASel, BrUn, ImmSel, RegWEn, RomPCSel}));
  or or_1 (or_1_out, BrEq, BrLt);
  Multiplexer #(.enable("false")) multiplexer_1 (.in0(RomPCSel), .in1(or_1_out), .out(PCSel), .sel(brSel));

  // Other names for the same wires on the sheet: opcode[6:0] = inst[6:0]; func3[2:0] = inst[14:12];
  //   func7[6:0] = inst[31:25]

  // Notes on the sheet:
  //   INPUTS to your circuit
  //   contents of rom_1 (hex, n*v repeats v):
  //   0 0 0 82 15*0 2082 0 0 0 20d2 11*0 3084 15*0 2002 0 0 0 2d92 43*0 220c8 0 0 0 4083 7*0 40cf 19*0 82
  //   15*0 2682 0 0 0 20d2 11*0 3084 15*0 2602 0 0 0 2d92 43*0 220c8 11*0 40cf 0 0 0 10000 15*0 82 15*0
  //   2782 0 0 0 20d2 11*0 3084 15*0 2702 0 0 0 2d92 55*0 40cf 39*0 20d2 31*0 2d92 55*0 40cf 35*0 2382 0 0
  //   0 20d2 27*0 2302 0 0 0 2d92 43*0 220c8 11*0 40cf 35*0 2482 0 0 0 20d2 27*0 2402 0 0 0 2d92 43*0
  //   220c8 11*0 40cf 0 0 0 18000 31*0 2282 0 0 0 20d2 27*0 2202 0 0 0 2d92 43*0 220e8 11*0 40cf 35*0 2182
  //   0 0 0 20d2 27*0 2102 0 0 0 2d92 43*0 220e8 11*0 40cf 19*0 82 15*0 2082 0 0 0 20d2 11*0 3084 15*0
  //   2a02 0 0 0 2d92 43*0 220c8 0 0 0 4083 7*0 40cf 19*0 82 19*0 20d2 11*0 3084 15*0 2e02 0 0 0 2d92 43*0
  //   220c8 11*0 40cf 0 0 0 10000 15*0 82 15*0 2782 0 0 0 20d2 11*0 3084 19*0 2d92 55*0 40cf 39*0 20d2
  //   27*0 2b02 0 0 0 2d92 55*0 40cf 35*0 2382 0 0 0 20d2 31*0 2d92 43*0 220c8 11*0 40cf 39*0 20d2 31*0
  //   2d92 43*0 220c8 11*0 40cf 0 0 0 18000 31*0 2282 0 0 0 20d2 31*0 2d92 43*0 220e8 11*0 40cf 35*0 2182
  //   0 0 0 20d2 31*0 2d92 43*0 220e8 11*0 40cf 19*0 82 15*0 2082 0 0 0 20d2 11*0 3084 15*0 2c02 0 0 0
  //   2d92 43*0 220c8 0 0 0 4083 7*0 40cf 19*0 82 19*0 20d2 11*0 3084 19*0 2d92 43*0 220c8 11*0 40cf 0 0 0
  //   10000 15*0 82 15*0 2782 0 0 0 20d2 11*0 3084 19*0 2d92 55*0 40cf 39*0 20d2 31*0 2d92 55*0 40cf 35*0
  //   2382 0 0 0 20d2 31*0 2d92 43*0 220c8 11*0 40cf 35*0 2582 0 0 0 20d2 27*0 2502 0 0 0 2d92 43*0 220c8
  //   11*0 40cf 0 0 0 18000 31*0 2282 0 0 0 20d2 31*0 2d92 43*0 220e8 11*0 40cf 35*0 2182 0 0 0 20d2 31*0
  //   2d92 43*0 220e8 11*0 40cf 19*0 82 15*0 2082 0 0 0 20d2 11*0 3084 19*0 2d92 43*0 220c8 0 0 0 4083 7*0
  //   40cf 19*0 82 19*0 20d2 11*0 3084 19*0 2d92 43*0 220c8 11*0 40cf 0 0 0 10000 15*0 82 15*0 2782 0 0 0
  //   20d2 11*0 3084 19*0 2d92 55*0 40cf 39*0 20d2 31*0 2d92 55*0 40cf 35*0 2382 0 0 0 20d2 31*0 2d92 43*0
  //   220c8 11*0 40cf 39*0 20d2 31*0 2d92 43*0 220c8 11*0 40cf 0 0 0 18000 31*0 2282 0 0 0 20d2 31*0 2d92
  //   43*0 220e8 11*0 40cf 35*0 2182 0 0 0 20d2 31*0 2d92 43*0 220e8 11*0 40cf
  //   DON'T CHANGE THE LOCATIONS OF THE INPUTS AND OUTPUTS!
  //   OUTPUT from your circuit
endmodule
