// Logisim project cpu.circ as structural Verilog: 1 circuit, main circuit cpu
module cpu (
  input  clk,
  input  [31:0] INSTRUCTION,
  input  [31:0] READ_DATA,
  output [31:0] WRITE_ADDRESS,
  output [31:0] PROGRAM_COUNTER,
  output [31:0] ra,
  output [31:0] sp,
  output [31:0] t0,
  output [31:0] t1,
  output [31:0] t2,
  output [31:0] s0,
  output [31:0] s1,
  output [31:0] a0,
  output [31:0] tohost,
  output [3:0] WRITE_ENABLE,
  output [31:0] WRITE_DATA
);

  wire ASel, brEq, brLt, brUn, BSel, CSRSel, CSRWen, MemRw, PCSel, RegWEn;
  wire [0:0] alu_out;
  wire [1:0] WBSel;
  wire [2:0] funct3, ImmSel;
  wire [3:0] ALUSel, bit_extender_4_out, multiplexer_8_out, shifter_3_out;
  wire [4:0] rd, rs1;
  wire [6:0] INST_ID_q;
  wire [7:0] shifter_2_out;
  wire [11:0] CSR_address;
  wire [15:8] shifter_2_out_2;
  wire [31:0] adder_1_out, adder_2_out, bit_extender_1_out, bit_extender_2_out, bit_extender_3_out, imm32,
       multiplexer_1_out, multiplexer_2_out, multiplexer_3_out, multiplexer_4_out, multiplexer_5_out,
       multiplexer_6_out, PC, rs1_data, WB_DATA;
  wire [31:1] alu_address;
  wire [31:16] shifter_2_out_3;

  Adder #(.width(32)) adder_1 (.a(PROGRAM_COUNTER), .b(32'h4), .out(adder_1_out));  // open: cin, cout
  Register #(.width(32)) u_PC (.D(multiplexer_1_out), .en(1'b1), .clk(clk), .Q(PROGRAM_COUNTER));  // open: clr
  Multiplexer #(.enable("false"), .width(32)) multiplexer_1 (
    .in0(adder_1_out), .in1({alu_address, 1'b0}), .out(multiplexer_1_out), .sel(PCSel));
  Register #(.width(32)) PC_ID (.D(PROGRAM_COUNTER), .en(1'b1), .clk(clk), .Q(PC));  // open: clr
  Register #(.width(32)) INST_ID (
    .D(multiplexer_2_out), .en(1'b1), .clk(clk), .Q({CSR_address, rs1, funct3, rd, INST_ID_q}));  // open: clr
  Multiplexer #(.enable("false"), .width(32)) multiplexer_2 (
    .in0(INSTRUCTION), .in1(32'h13), .out(multiplexer_2_out), .sel(PCSel));
  control_logic control_logic_1 (
    .CSRWen(CSRWen), .PCSel(PCSel), .RegWEn(RegWEn), .ImmSel(ImmSel), .BrUn(brUn), .ASel(ASel), .BSel(BSel),
    .ALUSel(ALUSel), .MemRW(MemRw), .WBSel(WBSel), .CSRSel(CSRSel),
    .inst({CSR_address, rs1, funct3, rd, INST_ID_q}), .BrEq(brEq), .BrLt(brLt));
  imm_gen imm_gen_1 (.inst({CSR_address, rs1, funct3, rd, INST_ID_q}), .ImmSel(ImmSel), .imm(imm32));
  regfile regfile_1 (
    .rs1(rs1), .rs2(CSR_address[4:0]), .rd(rd), .Write_Data(WB_DATA), .RegWEn(RegWEn), .clk(clk), .ra(ra),
    .sp(sp), .t0(t0), .t1(t1), .t2(t2), .s0(s0), .s1(s1), .a0(a0), .Read_Data_1(rs1_data),
    .Read_Data_2(WRITE_DATA));
  assign bit_extender_1_out = {{27{1'b0}}, rs1};  // Bit_Extender bit_extender_1
  Multiplexer #(.enable("false"), .width(32)) multiplexer_3 (
    .in0(rs1_data), .in1(bit_extender_1_out), .out(multiplexer_3_out), .sel(CSRSel));
  branch_comp branch_comp_1 (.rs1(rs1_data), .rs2(WRITE_DATA), .BrUn(brUn), .BrEq(brEq), .BrLt(brLt));
  csr csr_1 (.CSR_address(CSR_address), .CSR_din(multiplexer_3_out), .CSR_WE(CSRWen), .clk(clk), .tohost(tohost));
  Multiplexer #(.enable("false"), .width(32)) multiplexer_4 (
    .in0(rs1_data), .in1(PC), .out(multiplexer_4_out), .sel(ASel));
  Multiplexer #(.enable("false"), .width(32)) multiplexer_5 (
    .in0(WRITE_DATA), .in1(imm32), .out(multiplexer_5_out), .sel(BSel));
  alu alu_1 (.Result({alu_address, alu_out[0]}), .A(multiplexer_4_out), .B(multiplexer_5_out), .ALUSel(ALUSel));
  Shifter #(.width(32)) shifter_1 (
    .in({alu_address, alu_out[0]}), .\dist ({alu_address[1], alu_out[0], 3'b000}), .out(WRITE_ADDRESS));
  Shifter #(.shift("lr"), .width(32)) shifter_2 (
    .in(READ_DATA), .\dist ({alu_address[1], alu_out[0], 3'b000}),
    .out({shifter_2_out_3, shifter_2_out_2, shifter_2_out}));
  assign bit_extender_2_out = {{24{shifter_2_out[7]}}, shifter_2_out};  // Bit_Extender bit_extender_2
  assign bit_extender_3_out = {{16{shifter_2_out_2[15]}}, {shifter_2_out_2, shifter_2_out}};  // Bit_Extender bit_extender_3
  Multiplexer #(.enable("false"), .select(2), .width(32)) multiplexer_6 (
    .in0(bit_extender_2_out), .in1(bit_extender_3_out),
    .in2({shifter_2_out_3, shifter_2_out_2, shifter_2_out}), .out(multiplexer_6_out), .sel(funct3[1:0]));  // open: in3
  Multiplexer #(.enable("false"), .select(2), .width(32)) multiplexer_7 (
    .in0(multiplexer_6_out), .in1({alu_address, alu_out[0]}), .in2(adder_2_out), .out(WB_DATA), .sel(WBSel));  // open: in3
  Adder #(.width(32)) adder_2 (.a(32'h4), .b(PC), .out(adder_2_out));  // open: cin, cout
  Multiplexer #(.enable("false"), .select(2), .width(4)) multiplexer_8 (
    .in0(4'b0001), .in1(4'b0011), .in2(4'b1111), .out(multiplexer_8_out), .sel(funct3[1:0]));  // open: in3
  assign bit_extender_4_out = {{3{MemRw}}, MemRw};  // Bit_Extender bit_extender_4
  Shifter #(.width(4)) shifter_3 (.in(multiplexer_8_out), .\dist ({alu_address[1], alu_out[0]}), .out(shifter_3_out));
  assign WRITE_ENABLE = bit_extender_4_out & shifter_3_out;  // AND_Gate and_1, 4 bits wide

  // Other names for the same wires on the sheet: rs2[4:0] = CSR_address[4:0]; alu_out[31:1] = alu_address;
  //   rs2_data[31:0] = WRITE_DATA; low_2bits[1:0] = {alu_address[1], alu_out[0]};
  //   shift_bits[4:3] = {alu_address[1], alu_out[0]}

  // Notes on the sheet:
  //   Output to IMEM
  //   IMEM
  //   Inputs from IMEM
  //   Inputs/Outputs for testing
  //   Outputs To DMEM
  //   DMEM
  //   Inputs From DMEM
endmodule
