// Logisim project imm_gen.circ as structural Verilog: 1 circuit, main circuit imm_gen
module imm_gen (
  input  [31:0] inst,
  input  [2:0] ImmSel,
  output [31:0] imm
);

  wire [11:0] imm12;
  wire [31:0] bit_extender_1_out, bit_extender_2_out, instB, instI, instJ, instS, instU;

  Demultiplexer #(.enable("false"), .select(3), .width(32)) demultiplexer_1 (
    .out0(instI), .out1(instS), .out2(instB), .out3(instJ), .out4(instU), .in(inst), .sel(ImmSel));  // open: out5, out6, out7
  assign bit_extender_1_out = {{20{1'b0}}, imm12};  // Bit_Extender bit_extender_1
  assign bit_extender_2_out = {{20{imm12[11]}}, imm12};  // Bit_Extender bit_extender_2
  Multiplexer #(.enable("false"), .select(3), .width(32)) multiplexer_1 (
    .in0(bit_extender_1_out), .in1(bit_extender_2_out), .out(imm), .sel(ImmSel));  // open: in2, in3, in4, in5, in6, in7

  // Other names for the same wires on the sheet: immS[11:0] = {inst[31:25], inst[11:7]}; immI[11:0] = inst[31:20]

  // Notes on the sheet:
  //   INPUTS to your circuit
  //   DON'T CHANGE THE LOCATIONS OF THE INPUTS AND OUTPUTS!
  //   OUTPUT from your circuit
endmodule
