// Logisim project regfile.circ as structural Verilog: 1 circuit, main circuit regfile
module regfile (
  input  [4:0] rs1,
  input  [4:0] rs2,
  input  [4:0] rd,
  input  [31:0] Write_Data,
  input  RegWEn,
  input  clk,
  output [31:0] ra,
  output [31:0] sp,
  output [31:0] t0,
  output [31:0] t1,
  output [31:0] t2,
  output [31:0] s0,
  output [31:0] s1,
  output [31:0] a0,
  output [31:0] Read_Data_1,
  output [31:0] Read_Data_2
);

  wire select_en0, select_en1, select_en2, select_en3, select_en4, select_en5, select_en6, select_en7,
       select_en8, select_en9, select_en10, select_en11, select_en12, select_en13, select_en14, select_en15,
       select_en16, select_en17, select_en18, select_en19, select_en20, select_en21, select_en22,
       select_en23, select_en24, select_en25, select_en26, select_en27, select_en28, select_en29,
       select_en30, select_en31;
  wire [31:0] x3, x4, x11, x12, x13, x14, x15, x16, x17, x18, x19, x20, x21, x22, x23, x24, x25, x26, x27,
       x28, x29, x30, x31;

  Register #(.width(32)) reg1 (.D(Write_Data), .en(select_en1), .clk(clk), .Q(ra));  // open: clr
  Register #(.width(32)) reg2 (.D(Write_Data), .en(select_en2), .clk(clk), .Q(sp));  // open: clr
  Register #(.width(32)) reg3 (.D(Write_Data), .en(select_en3), .clk(clk), .Q(x3));  // open: clr
  Register #(.width(32)) reg4 (.D(Write_Data), .en(select_en4), .clk(clk), .Q(x4));  // open: clr
  Register #(.width(32)) reg5 (.D(Write_Data), .en(select_en5), .clk(clk), .Q(t0));  // open: clr
  Register #(.width(32)) reg6 (.D(Write_Data), .en(select_en6), .clk(clk), .Q(t1));  // open: clr
  Register #(.width(32)) reg7 (.D(Write_Data), .en(select_en7), .clk(clk), .Q(t2));  // open: clr
  Demultiplexer #(.enable("false"), .select(5)) demultiplexer_1 (
    .out0(select_en0), .out1(select_en1), .out2(select_en2), .out3(select_en3), .out4(select_en4),
    .out5(select_en5), .out6(select_en6), .out7(select_en7), .out8(select_en8), .out9(select_en9),
    .out10(select_en10), .out11(select_en11), .out12(select_en12), .out13(select_en13), .out14(select_en14),
    .out15(select_en15), .out16(select_en16), .out17(select_en17), .out18(select_en18), .out19(select_en19),
    .out20(select_en20), .out21(select_en21), .out22(select_en22), .out23(select_en23), .out24(select_en24),
    .out25(select_en25), .out26(select_en26), .out27(select_en27), .out28(select_en28), .out29(select_en29),
    .out30(select_en30), .out31(select_en31), .in(RegWEn), .sel(rd));
  Multiplexer #(.enable("false"), .select(5), .width(32)) multiplexer_1 (
    .in0({32{1'b0}}), .in1(ra), .in2(sp), .in3(x3), .in4(x4), .in5(t0), .in6(t1), .in7(t2), .in8(s0),
    .in9(s1), .in10(a0), .in11(x11), .in12(x12), .in13(x13), .in14(x14), .in15(x15), .in16(x16), .in17(x17),
    .in18(x18), .in19(x19), .in20(x20), .in21(x21), .in22(x22), .in23(x23), .in24(x24), .in25(x25),
    .in26(x26), .in27(x27), .in28(x28), .in29(x29), .in30(x30), .in31(x31), .out(Read_Data_1), .sel(rs1));
  Register #(.width(32)) reg8 (.D(Write_Data), .en(select_en8), .clk(clk), .Q(s0));  // open: clr
  Register #(.width(32)) reg9 (.D(Write_Data), .en(select_en9), .clk(clk), .Q(s1));  // open: clr
  Register #(.width(32)) reg10 (.D(Write_Data), .en(select_en10), .clk(clk), .Q(a0));  // open: clr
  Register #(.width(32)) reg11 (.D(Write_Data), .en(select_en11), .clk(clk), .Q(x11));  // open: clr
  Register #(.width(32)) reg12 (.D(Write_Data), .en(select_en12), .clk(clk), .Q(x12));  // open: clr
  Register #(.width(32)) reg13 (.D(Write_Data), .en(select_en13), .clk(clk), .Q(x13));  // open: clr
  Register #(.width(32)) reg14 (.D(Write_Data), .en(select_en14), .clk(clk), .Q(x14));  // open: clr
  Register #(.width(32)) reg15 (.D(Write_Data), .en(select_en15), .clk(clk), .Q(x15));  // open: clr
  Multiplexer #(.enable("false"), .select(5), .width(32)) multiplexer_2 (
    .in0({32{1'b0}}), .in1(ra), .in2(sp), .in3(x3), .in4(x4), .in5(t0), .in6(t1), .in7(t2), .in8(s0),
    .in9(s1), .in10(a0), .in11(x11), .in12(x12), .in13(x13), .in14(x14), .in15(x15), .in16(x16), .in17(x17),
    .in18(x18), .in19(x19), .in20(x20), .in21(x21), .in22(x22), .in23(x23), .in24(x24), .in25(x25),
    .in26(x26), .in27(x27), .in28(x28), .in29(x29), .in30(x30), .in31(x31), .out(Read_Data_2), .sel(rs2));
  Register #(.width(32)) reg16 (.D(Write_Data), .en(select_en16), .clk(clk), .Q(x16));  // open: clr
  Register #(.width(32)) reg17 (.D(Write_Data), .en(select_en17), .clk(clk), .Q(x17));  // open: clr
  Register #(.width(32)) reg18 (.D(Write_Data), .en(select_en18), .clk(clk), .Q(x18));  // open: clr
  Register #(.width(32)) reg19 (.D(Write_Data), .en(select_en19), .clk(clk), .Q(x19));  // open: clr
  Register #(.width(32)) reg20 (.D(Write_Data), .en(select_en20), .clk(clk), .Q(x20));  // open: clr
  Register #(.width(32)) reg21 (.D(Write_Data), .en(select_en21), .clk(clk), .Q(x21));  // open: clr
  Register #(.width(32)) reg22 (.D(Write_Data), .en(select_en22), .clk(clk), .Q(x22));  // open: clr
  Register #(.width(32)) reg23 (.D(Write_Data), .en(select_en23), .clk(clk), .Q(x23));  // open: clr
  Register #(.width(32)) reg24 (.D(Write_Data), .en(select_en24), .clk(clk), .Q(x24));  // open: clr
  Register #(.width(32)) reg25 (.D(Write_Data), .en(select_en25), .clk(clk), .Q(x25));  // open: clr
  Register #(.width(32)) reg26 (.D(Write_Data), .en(select_en26), .clk(clk), .Q(x26));  // open: clr
  Register #(.width(32)) reg27 (.D(Write_Data), .en(select_en27), .clk(clk), .Q(x27));  // open: clr
  Register #(.width(32)) reg28 (.D(Write_Data), .en(select_en28), .clk(clk), .Q(x28));  // open: clr
  Register #(.width(32)) reg29 (.D(Write_Data), .en(select_en29), .clk(clk), .Q(x29));  // open: clr
  Register #(.width(32)) reg30 (.D(Write_Data), .en(select_en30), .clk(clk), .Q(x30));  // open: clr
  Register #(.width(32)) reg31 (.D(Write_Data), .en(select_en31), .clk(clk), .Q(x31));  // open: clr

  // Other names for the same wires on the sheet: read_data1[31:0] = Read_Data_1; read_data2[31:0] = Read_Data_2;
  //   read_reg1[4:0] = rs1; read_reg2[4:0] = rs2; write_en = RegWEn; write_reg[4:0] = rd; x1[31:0] = ra;
  //   x2[31:0] = sp; x5[31:0] = t0; x6[31:0] = t1; x7[31:0] = t2; x8[31:0] = s0; x9[31:0] = s1; x10[31:0] = a0

  // Notes on the sheet:
  //   INPUTS to your circuit
  //   DON'T CHANGE THE LOCATIONS OF THE INPUTS AND OUTPUTS!
  //   These are DEBUG/TEST outputs from your circuit.
  //   OUTPUTS from your circuit
endmodule
